# Fritzing sketch radar (saved by Fritzing 0.9.3b)
breadboards: 1

parts:
  R1 = Resistor [tolerance=±5% resistance=220 package="1206 [SMD]"]
  LED1 = LED - 5mm [color="Red (633nm)" package="5 mm [THT]"]
  LED2 = LED - 5mm [color="Yellow (585nm)" package="5 mm [THT]"]
  R2 = Resistor [tolerance=±5% resistance=220 package="1206 [SMD]"]
  LED3 = LED - 5mm [color="Green (555nm)" package="5 mm [THT]"]
  R3 = Resistor [tolerance=±1% resistance=220 package="1206 [SMD]"]
  Part1 = Arduino Uno (Rev3)
  J1 = Piezo Speaker
  Sensor1 = HC-SR04 Ultrasonic Distance Sensor
  J2 = Basic Servo

nets:
  N1: R1.Pin_0, LED1.cathode
  GND: R1.Pin_1, R2.Pin_1, R3.Pin_1, Part1.GND, J1.pin1, Sensor1.GND, J2.gnd
  N2: LED1.anode, Part1.D5_PWM
  N3: LED2.cathode, R2.Pin_0
  N4: LED2.anode, Part1.D4
  N5: LED3.cathode, R3.Pin_0
  N6: LED3.anode, Part1.D3_PWM
  N7: Part1.D10_PWM/SS, Sensor1.TRIG
  N8: Part1.D11_PWM/MOSI, Sensor1.ECHO
  N9: Part1.D12/MISO, J2.pulse
  N10: Part1.D7, J1.pin2
  VCC: Part1.5V, Sensor1.VCC, J2.vcc

custom parts:
  HC-SR04 Ultrasonic Distance Sensor: The HC-SR04 is an ultrasonic distance sensor. It is capable of providing measurement for ranges of 2cm to 400cm. The module operates at 5V.
